// Digital circuit CU_RF.dig as structural Verilog
module CU_RF (
  input  [25:0] EX_WB,
  input  CLK,
  input  [15:0] IF_ID,
  output [59:0] ID_EX,
  output [15:0] IF
);

  wire [3:1] FL_q;

  Register #(.Bits(4)) FL (.D(EX_WB[9:6]), .C(CLK), .en(EX_WB[5]), .Q({FL_q, ID_EX[59]}));
  control_unit_new control_unit_new_1 (
    .INST(IF_ID), .RS1(ID_EX[54:52]), .RS2(ID_EX[57:55]), .WS(ID_EX[2:0]), .WE(ID_EX[3]), .SETH(ID_EX[4]),
    .FLEN(ID_EX[5]), .ALUOP(ID_EX[7:6]), .DMUX(ID_EX[9:8]), .STR(ID_EX[10]), .LDR(ID_EX[11]), .COND(ID_EX[58]));
  reg_file reg_file_1 (
    .WS(EX_WB[2:0]), .WE(EX_WB[3]), .SETH(EX_WB[4]), .IN(EX_WB[25:10]), .Flag({FL_q, ID_EX[59]}), .clk(CLK),
    .RS1(ID_EX[54:52]), .RS2(ID_EX[57:55]), .pc(IF), .OUT1(ID_EX[27:12]), .OUT2(ID_EX[43:28]));

  assign ID_EX[51:44] = IF_ID[7:0];
endmodule
