// Digital circuit EX-ID_forward_logic.dig as structural Verilog
module EX_ID_forward_logic (
  input  [3:0] Flag,
  input  SETH,
  input  [15:0] \new ,
  input  FLEN,
  input  WE,
  input  [2:0] WS,
  input  [15:0] old,
  input  [2:0] RS,
  output FORWARDED
);

  wire and_1_out, eq_1_eq, eq_2_eq, eq_3_eq, multiplexer_2_out, multiplexer_3_out, not_1_out;
  wire [15:0] multiplexer_1_out;

  eq eq_1 (.A(WS), .B(RS), .EQ(eq_1_eq));
  eq eq_2 (.A(3'b000), .B(RS), .EQ(eq_2_eq));
  not not_1 (not_1_out, eq_2_eq);
  and and_1 (and_1_out, eq_1_eq, WE, not_1_out);
  Multiplexer #(.Bits(16)) multiplexer_1 (
    .sel(SETH), .in_0(\new ), .in_1({\new [7:0], old[7:0]}), .out(multiplexer_1_out));
  Multiplexer multiplexer_2 (.sel(and_1_out), .in_0(old[0]), .in_1(multiplexer_1_out[0]), .out(multiplexer_2_out));
  Multiplexer multiplexer_3 (.sel(FLEN), .in_0(old[0]), .in_1(Flag[0]), .out(multiplexer_3_out));
  eq eq_3 (.A(RS), .B(3'b101), .EQ(eq_3_eq));
  Multiplexer multiplexer_4 (.sel(eq_3_eq), .in_0(multiplexer_2_out), .in_1(multiplexer_3_out), .out(FORWARDED));
  // Pins of 1 and 3 bits meet at RS
  // Pins of 1 and 16 bits meet at {{12{1'b0}}, Flag}
  // Pins of 1 and 16 bits meet at old
  // Pins of 1 and 16 bits meet at \new 
  // Pins of 1 and 16 bits meet at multiplexer_1_out
  // Pins of 1 and 3 bits meet at WS
endmodule
