// Digital circuit Harz_Resl.dig as structural Verilog
module Harz_Resl (
  input  [25:0] EX_WB,
  input  [59:0] ID,
  input  [15:0] PC,
  output [51:0] ID_EX,
  output [15:0] IF,
  output JMP
);

  wire and_2_out, and_3_out, and_4_out, eq_1_eq, eq_2_eq, eq_3_eq, eq_4_eq, eq_5_eq, eq_6_eq, eq_7_eq,
       multiplexer_1_out, not_1_out, not_2_out, not_3_out, or_1_out;
  wire [15:0] multiplexer_2_out, multiplexer_3_out, multiplexer_4_out, multiplexer_5_out, multiplexer_6_out,
       multiplexer_7_out, multiplexer_8_out;

  eq eq_1 (.A(3'b111), .B(EX_WB[2:0]), .EQ(eq_1_eq));
  Multiplexer multiplexer_1 (.sel(EX_WB[5]), .in_0(ID[59]), .in_1(EX_WB[6]), .out(multiplexer_1_out));
  eq eq_2 (.A(3'b000), .B(ID[54:52]), .EQ(eq_2_eq));
  eq eq_3 (.A(3'b000), .B(ID[57:55]), .EQ(eq_3_eq));
  and and_1 (JMP, eq_1_eq, EX_WB[3]);
  eq eq_4 (.A(EX_WB[2:0]), .B(ID[54:52]), .EQ(eq_4_eq));
  not not_1 (not_1_out, eq_2_eq);
  Multiplexer #(.Bits(16)) multiplexer_2 (
    .sel(EX_WB[4]), .in_0(EX_WB[25:10]), .in_1({EX_WB[17:10], ID[19:12]}), .out(multiplexer_2_out));
  eq eq_5 (.A(EX_WB[2:0]), .B(ID[57:55]), .EQ(eq_5_eq));
  not not_2 (not_2_out, eq_3_eq);
  Multiplexer #(.Bits(16)) multiplexer_3 (
    .sel(EX_WB[4]), .in_0(EX_WB[25:10]), .in_1({EX_WB[17:10], ID[35:28]}), .out(multiplexer_3_out));
  or or_1 (or_1_out, ~ID[58], multiplexer_1_out);  // Or
  and and_2 (and_2_out, eq_4_eq, EX_WB[3], not_1_out);
  and and_3 (and_3_out, eq_5_eq, EX_WB[3], not_2_out);
  not not_3 (not_3_out, JMP);
  and and_4 (and_4_out, not_3_out, or_1_out);
  eq eq_6 (.A(ID[54:52]), .B(3'b101), .EQ(eq_6_eq));
  Multiplexer #(.Bits(16)) multiplexer_4 (
    .sel(and_2_out), .in_0(ID[27:12]), .in_1(multiplexer_2_out), .out(multiplexer_4_out));
  Multiplexer #(.Bits(16)) multiplexer_5 (
    .sel(EX_WB[5]), .in_0(ID[27:12]), .in_1({{12{1'b0}}, EX_WB[9:6]}), .out(multiplexer_5_out));
  eq eq_7 (.A(ID[57:55]), .B(3'b101), .EQ(eq_7_eq));
  Multiplexer #(.Bits(16)) multiplexer_6 (
    .sel(and_3_out), .in_0(ID[43:28]), .in_1(multiplexer_3_out), .out(multiplexer_6_out));
  Multiplexer #(.Bits(16)) multiplexer_7 (
    .sel(EX_WB[5]), .in_0(ID[43:28]), .in_1({{12{1'b0}}, EX_WB[9:6]}), .out(multiplexer_7_out));
  Multiplexer #(.Bits(16)) multiplexer_8 (
    .sel(EX_WB[4]), .in_0(EX_WB[25:10]), .in_1({EX_WB[17:10], PC[7:0]}), .out(multiplexer_8_out));
  Multiplexer #(.Bits(12)) multiplexer_9 (.sel(and_4_out), .in_0({12{1'b0}}), .in_1(ID[11:0]), .out(ID_EX[11:0]));
  Multiplexer #(.Bits(16)) multiplexer_10 (
    .sel(eq_6_eq), .in_0(multiplexer_4_out), .in_1(multiplexer_5_out), .out(ID_EX[27:12]));
  Multiplexer #(.Bits(16)) multiplexer_11 (
    .sel(eq_7_eq), .in_0(multiplexer_6_out), .in_1(multiplexer_7_out), .out(ID_EX[43:28]));
  Multiplexer #(.Bits(16)) multiplexer_12 (.sel(JMP), .in_0(PC), .in_1(multiplexer_8_out), .out(IF));

  assign ID_EX[51:44] = ID[51:44];
endmodule
