// Digital circuit RAM_ALU.dig as structural Verilog
module RAM_ALU (
  input  [15:0] IF,
  input  CLK,
  input  [51:0] ID_EX,
  output [15:0] IF_ID,
  output [25:0] EX_WB
);

  wire [15:0] alu_1_result, notconnected_1_out, RAM_d1;

  RAMDualAccess #(.AddrBits(16), .isProgramMemory("true"), .Bits(16)) RAM (
    .str(ID_EX[42]), .C(CLK), .ld(ID_EX[43]), .A1(ID_EX[15:0]), .Din1(ID_EX[31:16]), .A2(IF), .D1(RAM_d1),
    .D2(IF_ID));
  alu alu_1 (.A(ID_EX[15:0]), .B(ID_EX[31:16]), .ALUOP(ID_EX[39:38]), .FLAG(EX_WB[9:6]), .RESULT(alu_1_result));
  Multiplexer #(.Selector_Bits(2), .Bits(16)) multiplexer_1 (
    .sel(ID_EX[41:40]), .in_0(alu_1_result), .in_1(RAM_d1), .in_2({{8{1'b0}}, ID_EX[51:44]}),
    .in_3(notconnected_1_out), .out(EX_WB[25:10]));
  // NotConnected on notconnected_1_out
  // Probe DATA on EX_WB[25:10]

  assign EX_WB[5:0] = ID_EX[37:32];
endmodule
