// Digital circuit cpu.dig as structural Verilog
module cpu (
  input  CLK
);

  wire harz_resl_1_jmp, not_1_out, not_2_out, not_3_out, not_4_out;
  wire [15:0] alu_1_result, cu_rf_1_if, harz_resl_1_if, IF_ID_q, IF_q, multiplexer_1_out, notconnected_1_out,
       ramdualaccess_1_d1, ramdualaccess_1_d2;
  wire [25:0] EX_WB_q;
  wire [25:6] alu_1_flag;
  wire [51:0] harz_resl_1_id_ex, ID_EX_q;
  wire [59:0] cu_rf_1_id_ex;

  CU_RF cu_rf_1 (.EX_WB(EX_WB_q), .CLK(CLK), .IF_ID(IF_ID_q), .ID_EX(cu_rf_1_id_ex), .IF(cu_rf_1_if));
  Register #(.Bits(26)) EX_WB (.D({alu_1_flag, ID_EX_q[5:0]}), .C(not_1_out), .en(1'b1), .Q(EX_WB_q));
  not not_1 (not_1_out, CLK);
  Harz_Resl harz_resl_1 (
    .EX_WB({alu_1_flag, ID_EX_q[5:0]}), .ID(cu_rf_1_id_ex), .PC(cu_rf_1_if), .ID_EX(harz_resl_1_id_ex),
    .IF(harz_resl_1_if), .JMP(harz_resl_1_jmp));
  not not_2 (not_2_out, CLK);
  Register #(.Bits(16)) IF_ID (.D(multiplexer_1_out), .C(not_2_out), .en(1'b1), .Q(IF_ID_q));
  not not_3 (not_3_out, CLK);
  Multiplexer #(.Bits(16)) multiplexer_1 (
    .sel(harz_resl_1_jmp), .in_0(ramdualaccess_1_d2), .in_1({16{1'b0}}), .out(multiplexer_1_out));
  Register #(.Bits(52)) ID_EX (.D(harz_resl_1_id_ex), .C(not_3_out), .en(1'b1), .Q(ID_EX_q));
  not not_4 (not_4_out, CLK);
  Register #(.Bits(16)) IF (.D(harz_resl_1_if), .C(not_4_out), .en(1'b1), .Q(IF_q));
  RAMDualAccess #(.AddrBits(16), .isProgramMemory("true"), .Bits(16)) ramdualaccess_1 (
    .str(ID_EX_q[10]), .C(CLK), .ld(ID_EX_q[11]), .A1(ID_EX_q[27:12]), .Din1(ID_EX_q[43:28]), .A2(IF_q),
    .D1(ramdualaccess_1_d1), .D2(ramdualaccess_1_d2));
  alu alu_1 (
    .A(ID_EX_q[27:12]), .B(ID_EX_q[43:28]), .ALUOP(ID_EX_q[7:6]), .FLAG(alu_1_flag[9:6]),
    .RESULT(alu_1_result));
  // NotConnected on notconnected_1_out
  Multiplexer #(.Selector_Bits(2), .Bits(16)) multiplexer_2 (
    .sel(ID_EX_q[9:8]), .in_0(alu_1_result), .in_1(ramdualaccess_1_d1), .in_2({{8{1'b0}}, ID_EX_q[51:44]}),
    .in_3(notconnected_1_out), .out(alu_1_flag[25:10]));
  // Probe DATA on alu_1_flag[25:10]
endmodule
