// Digital circuit eq.dig as structural Verilog
module eq (
  input  [2:0] A,
  input  [2:0] B,
  output EQ
);

  wire [2:0] xnor_1_out;

  assign xnor_1_out = ~(A ^ B);  // XNOr xnor_1, 3 bits wide
  and and_1 (EQ, xnor_1_out[0], xnor_1_out[1], xnor_1_out[2]);
endmodule
