// Digital circuit cpu.dig as structural Verilog
module cpu (
  input  CLK
);

  wire control_unit_1_exec, Flen, Seth;
  wire [1:0] control_unit_1_aluop, control_unit_1_str, DMUX;
  wire [3:0] alu_1_flag, FL_q;
  wire [9:0] Reg;
  wire [15:0] alu_1_result, multiplexer_1_out, notconnected_1_out, RAM_d1, RAM_d2, reg_file_1_out1,
       reg_file_1_out2, reg_file_1_pc;

  Register #(.Bits(4)) FL (.D(alu_1_flag), .C(CLK), .en(Flen), .Q(FL_q));
  // NotConnected on notconnected_1_out
  Multiplexer #(.Selector_Bits(2), .Bits(16)) multiplexer_1 (
    .sel(DMUX), .in_0(alu_1_result), .in_1(RAM_d1), .in_2({{8{1'b0}}, RAM_d2[7:0]}),
    .in_3(notconnected_1_out), .out(multiplexer_1_out));
  // Probe DATA on multiplexer_1_out
  reg_file reg_file_1 (
    .RS1(Reg[2:0]), .RS2(Reg[5:3]), .WS(Reg[8:6]), .WE(Reg[9]), .IN(multiplexer_1_out), .clk(CLK),
    .Flag(FL_q), .SETH(Seth), .OUT1(reg_file_1_out1), .OUT2(reg_file_1_out2), .pc(reg_file_1_pc));
  alu alu_1 (
    .A(reg_file_1_out1), .B(reg_file_1_out2), .ALUOP(control_unit_1_aluop), .RESULT(alu_1_result),
    .FLAG(alu_1_flag));
  RAMDualAccess #(.AddrBits(16), .isProgramMemory("true"), .Bits(16)) RAM (
    .str(control_unit_1_str[0]), .C(CLK), .ld(control_unit_1_str[1]), .A1(reg_file_1_out1),
    .Din1(reg_file_1_out2), .A2(reg_file_1_pc), .D1(RAM_d1), .D2(RAM_d2));
  control_unit control_unit_1 (
    .INST(RAM_d2), .Z(FL_q[0]), .ALUOP(control_unit_1_aluop), .RS1(Reg[2:0]), .RS2(Reg[5:3]), .WS(Reg[8:6]),
    .STR(control_unit_1_str[0]), .WE(Reg[9]), .DMUX(DMUX), .LDR(control_unit_1_str[1]), .FLEN(Flen),
    .EXEC(control_unit_1_exec), .SETH(Seth));
  LED Exec (.in(control_unit_1_exec));
endmodule
