// Digital circuit reg_file.dig as structural Verilog
module reg_file (
  input  [2:0] RS1,
  input  [2:0] RS2,
  input  [2:0] WS,
  input  WE,
  input  [15:0] IN,
  input  clk,
  input  [3:0] Flag,
  input  SETH,
  output [15:0] OUT1,
  output [15:0] OUT2,
  output [15:0] pc
);

  wire decoder_1_out_1, decoder_1_out_2, decoder_1_out_3, decoder_1_out_4, decoder_1_out_7, not_1_out;
  wire [7:0] add_1_s;
  wire [15:0] multiplexer_1_out, multiplexer_2_out, multiplexer_3_out, multiplexer_4_out, multiplexer_5_out,
       multiplexer_6_out, multiplexer_7_out, multiplexer_8_out, multiplexer_9_out, multiplexer_10_out, R1_q,
       R2_q, R3_q, R4_q;
  wire [15:8] add_1_s_2;

  not not_1 (not_1_out, SETH);
  Multiplexer #(.Bits(16)) multiplexer_1 (
    .sel(not_1_out), .in_0({IN[7:0], add_1_s}), .in_1(IN), .out(multiplexer_1_out));
  Multiplexer #(.Bits(16)) multiplexer_2 (
    .sel(decoder_1_out_7), .in_0({add_1_s_2, add_1_s}), .in_1(multiplexer_1_out), .out(multiplexer_2_out));
  Register #(.Bits(16)) u_PC (.D(multiplexer_2_out), .C(clk), .en(1'b1), .Q(pc));
  Add #(.Bits(16)) add_1 (.a(pc), .b(16'h1), .c_i(1'b0), .s({add_1_s_2, add_1_s}));  // open: c_o
  Multiplexer #(.Bits(16)) multiplexer_3 (
    .sel(not_1_out), .in_0({IN[7:0], R4_q[7:0]}), .in_1(IN), .out(multiplexer_3_out));
  Multiplexer #(.Bits(16)) multiplexer_4 (
    .sel(decoder_1_out_4), .in_0(R4_q), .in_1(multiplexer_3_out), .out(multiplexer_4_out));
  Register #(.Bits(16)) R4 (.D(multiplexer_4_out), .C(clk), .en(WE), .Q(R4_q));
  Multiplexer #(.Bits(16)) multiplexer_5 (
    .sel(not_1_out), .in_0({IN[7:0], R3_q[7:0]}), .in_1(IN), .out(multiplexer_5_out));
  Multiplexer #(.Bits(16)) multiplexer_6 (
    .sel(decoder_1_out_3), .in_0(R3_q), .in_1(multiplexer_5_out), .out(multiplexer_6_out));
  Register #(.Bits(16)) R3 (.D(multiplexer_6_out), .C(clk), .en(WE), .Q(R3_q));
  Multiplexer #(.Bits(16)) multiplexer_7 (
    .sel(not_1_out), .in_0({IN[7:0], R2_q[7:0]}), .in_1(IN), .out(multiplexer_7_out));
  Multiplexer #(.Bits(16)) multiplexer_8 (
    .sel(decoder_1_out_2), .in_0(R2_q), .in_1(multiplexer_7_out), .out(multiplexer_8_out));
  Register #(.Bits(16)) R2 (.D(multiplexer_8_out), .C(clk), .en(WE), .Q(R2_q));
  Decoder #(.Selector_Bits(3)) decoder_1 (
    .sel(WS), .out_1(decoder_1_out_1), .out_2(decoder_1_out_2), .out_3(decoder_1_out_3),
    .out_4(decoder_1_out_4), .out_7(decoder_1_out_7));  // open: out_0, out_5, out_6
  Multiplexer #(.Bits(16)) multiplexer_9 (
    .sel(not_1_out), .in_0({IN[7:0], R1_q[7:0]}), .in_1(IN), .out(multiplexer_9_out));
  Multiplexer #(.Bits(16)) multiplexer_10 (
    .sel(decoder_1_out_1), .in_0(R1_q), .in_1(multiplexer_9_out), .out(multiplexer_10_out));
  Register #(.Bits(16)) R1 (.D(multiplexer_10_out), .C(clk), .en(WE), .Q(R1_q));
  Multiplexer #(.Selector_Bits(3), .Bits(16)) multiplexer_11 (
    .sel(RS1), .in_0({16{1'b0}}), .in_1(R1_q), .in_2(R2_q), .in_3(R3_q), .in_4(R4_q),
    .in_5({{12{1'b0}}, Flag}), .in_6({16{1'b0}}), .in_7(pc), .out(OUT1));
  Multiplexer #(.Selector_Bits(3), .Bits(16)) multiplexer_12 (
    .sel(RS2), .in_0({16{1'b0}}), .in_1(R1_q), .in_2(R2_q), .in_3(R3_q), .in_4(R4_q),
    .in_5({{12{1'b0}}, Flag}), .in_6({16{1'b0}}), .in_7(pc), .out(OUT2));

  // Notes on the sheet:
  //   RS1: The index of the register which should output its value to OUT1.
  //   RS2: The index of the register which should output its value to OUT2.
  //   WS: The index of the register which should save the value on IN on the next clock cycle (if WE is high).
  //   WE: Whether the register selected by WS should save the value from IN on the next cycle.
  //   IN: The value to be saved into the register specified by WS if WE is high,
  //   OUT1: The value in the register specified by RS1.
  //   OUT2: The value in the register specified by RS2.
endmodule

/* Test case:
clk RS1 RS2 WS WE IN OUT1 OUT2
c 0 0 0 1 0x1234 0x0000 0x0000
c 1 0 1 1 0xBEEF 0xBEEF 0x0000
c 2 1 2 1 0xDEAD 0xDEAD 0xBEEF
c 3 2 3 1 0xFFFF 0xFFFF 0xDEAD
c 3 2 3 0 0xABCD 0xFFFF 0xDEAD
c 3 2 2 0 0xABCD 0xFFFF 0xDEAD
c 1 0 1 0 0xABCD 0xBEEF 0x0000
c 1 0 0 0 0xABCD 0xBEEF 0x0000
c 1 0 2 1 0xBADE 0xBEEF 0x0000
c 0 2 2 1 0xBADE 0x0000 0xBADE
c 0 0 2 0 0x1234 0x0000 0x0000
c 2 3 0 1 0x0000 0xBADE 0xFFFF
c 0 0 2 0 0x1234 0x0000 0x0000
*/
